// Logisim project 4 Bit Decrementor.circ as structural Verilog: 2 circuits, main circuit main
module main (
  input  Constant_1,
  input  Cin,
  input  A0,
  input  A1,
  input  A2,
  input  A3,
  output S0,
  output S1,
  output S3,
  output S4
);

  wire full_adder_1_cout, full_adder_2_cout, full_adder_3_cout, not_1_out;

  not not_1 (not_1_out, Cin);
  Full_Adder full_adder_1 (.Cin(not_1_out), .A(A0), .B(Constant_1), .S(S0), .Cout(full_adder_1_cout));
  Full_Adder full_adder_2 (.Cin(full_adder_1_cout), .A(A1), .B(Constant_1), .S(S1), .Cout(full_adder_2_cout));
  Full_Adder full_adder_3 (.Cin(full_adder_2_cout), .A(A2), .B(Constant_1), .S(S3), .Cout(full_adder_3_cout));
  Full_Adder full_adder_4 (.Cin(full_adder_3_cout), .A(A3), .B(Constant_1), .S(S4));  // open: Cout
endmodule

module Full_Adder (
  input  Cin,
  input  A,
  input  B,
  output S,
  output Cout
);

  wire and_1_out, and_2_out, xor_1_out;

  xor xor_1 (xor_1_out, A, B);
  xor xor_2 (S, xor_1_out, Cin);
  and and_1 (and_1_out, Cin, xor_1_out);
  and and_2 (and_2_out, A, B);
  xor xor_3 (Cout, and_1_out, and_2_out);
endmodule
